// Digital circuit ALU.dig as structural Verilog
module ALU (
  input  A1,
  input  B1,
  input  B2,
  input  B3,
  input  B4,
  input  B5,
  input  B6,
  input  B7,
  input  B8,
  input  A2,
  input  A3,
  input  A4,
  input  A5,
  input  A6,
  input  A7,
  input  A8,
  input  SEL1,
  input  SEL2,
  input  SEL3,
  input  SEL4,
  output Undf,
  output Overf,
  output [7:0] ALU_S
);

  wire AND1, AND2, AND3, AND4, AND5, AND6, AND7, AND8, LS1, LS2, LS3, LS4, LS5, LS6, LS7, LS8, M1, M2, M3,
       M4, M5, M6, M7, M8, OR1, OR2, OR3, OR4, OR5, OR6, OR7, OR8, RS1, RS2, RS3, RS4, RS5, RS6, RS7, RS8,
       S1, S2, S3, S4, S5, S6, S7, S8, SUB1, SUB2, SUB3, SUB4, SUB5, SUB6, SUB7, SUB8, XOR1, XOR2, XOR3,
       XOR4, XOR5, XOR6, XOR7, XOR8;

  // or_8bit OR: pin names not known; wires that end beside it: A1, B8, A2, B7, A3, B6, A4, B5, A5, B4, A6, B3, A7, B2, A8, B1, OR1, OR2, OR3, OR4, OR5, OR6, OR7, OR8
  // xor_8bit XOR: pin names not known; wires that end beside it: A1, B8, A2, B7, A3, B6, A4, B5, A5, B4, A6, B3, A7, B2, A8, B1, XOR1, XOR2, XOR3, XOR4, XOR5, XOR6, XOR7, XOR8
  // multiplier_4bit Multiplicador: pin names not known; wires that end beside it: B8, B7, B6, B5, A1, A2, A3, A4, M1, M2, M3, M4, M5, M6, M7, M8
  // and_8bit AND: pin names not known; wires that end beside it: A1, B8, A2, B7, A3, B6, A4, B5, A5, B4, A6, B3, A7, B2, A8, B1, AND1, AND2, AND3, AND4, AND5, AND6, AND7, AND8
  // subtractor_8bit Subtrator: pin names not known; wires that end beside it: A1, A2, A3, A4, A5, A6, A7, A8, B8, B7, B6, B5, B4, B3, B2, B1, SUB1, SUB2, SUB3, SUB4, SUB5, SUB6, SUB7, SUB8, Undf
  // adder_8bit Somador: pin names not known; wires that end beside it: A1, B8, A2, B7, A3, B6, A4, B5, A5, B4, A6, B3, A7, B2, A8, B1, S1, S2, S3, S4, S5, S6, S7, S8, Overf
  LED Underflow (.in(Undf));
  LED Overflow (.in(Overf));
  // right_shifter Right_shifter: pin names not known; wires that end beside it: A1, A2, A3, A4, A5, A6, A7, A8, RS8, RS7, RS6, RS5, RS4, RS3, RS2, RS1
  // left_shifter Left_shifter: pin names not known; wires that end beside it: A1, A2, A3, A4, A5, A6, A7, A8, LS8, LS7, LS6, LS5, LS4, LS3, LS2, LS1
  Multiplexer #(.Selector_Bits(4), .Bits(8)) multiplexer_1 (
    .sel({SEL4, SEL1, SEL2, SEL3}), .in_0({B1, B2, B3, B4, B5, B6, B7, B8}),
    .in_1({RS8, RS7, RS6, RS5, RS4, RS3, RS2, RS1}), .in_2({SUB8, SUB7, SUB6, SUB5, SUB4, SUB3, SUB2, SUB1}),
    .in_3({M8, M7, M6, M5, M4, M3, M2, M1}), .in_4({OR8, OR7, OR6, OR5, OR4, OR3, OR2, OR1}),
    .in_5({XOR8, XOR7, XOR6, XOR5, XOR4, XOR3, XOR2, XOR1}),
    .in_6({AND8, AND7, AND6, AND5, AND4, AND3, AND2, AND1}), .in_7({S8, S7, S6, S5, S4, S3, S2, S1}),
    .in_8({LS8, LS7, LS6, LS5, LS4, LS3, LS2, LS1}), .in_9({8{1'b0}}), .in_10({8{1'b0}}), .in_11({8{1'b0}}),
    .in_12({8{1'b0}}), .in_13({8{1'b0}}), .in_14({8{1'b0}}), .in_15({8{1'b0}}), .out(ALU_S));
  Seven_Seg_Hex seven_seg_hex_1 (.d(ALU_S[7:4]), .dp(1'b0));
  Seven_Seg_Hex seven_seg_hex_2 (.d(ALU_S[3:0]), .dp(1'b0));

  // Other names for the same wires on the sheet: B1_t = B8; B2_t = B7; B3_t = B6; B4_t = B5; B5_t = B4; B6_t = B3;
  //   B7_t = B2; B8_t = B1
endmodule
