// Digital circuit CPU.dig as structural Verilog
module CPU (
  input  Clock
);

  wire A1, A2, A3, A4, A5, A6, A7, A8, ALU_overf, ALU_undf, B1, B2, B3, B4, B5, B6, B7, B8, en, S1, S2, S3,
       S4;
  wire [3:0] D, PC;
  wire [7:0] ALU_alu_s;

  Seven_Seg_Hex seven_seg_hex_1 (.d(PC), .dp(1'b0));
  Seven_Seg_Hex seven_seg_hex_2 (.d({S4, S3, S2, S1}), .dp(1'b0));
  Seven_Seg_Hex seven_seg_hex_3 (.d({B4, B3, B2, B1}), .dp(1'b0));
  Register #(.Bits(4), .isProgramCounter("true")) Program_Counter (.D(D), .C(Clock), .en(en), .Q(PC));
  incrementador_8bits incrementador_8bits_1 (
    .A1(PC[0]), .A2(PC[1]), .A3(PC[2]), .A4(PC[3]), .S1(D[0]), .S2(D[1]), .S3(D[2]), .S4(D[3]));
  EEPROMDualPort #(.AddrBits(4), .Bits(12)) \Memória  (
    .A(PC), .Din({12{1'b0}}), .str(1'b1), .C(Clock), .ld(1'b1),
    .D({B8, B7, B6, B5, B4, B3, B2, B1, S4, S3, S2, S1}));
  Seven_Seg_Hex seven_seg_hex_4 (.d({B8, B7, B6, B5}), .dp(1'b0));
  ALU ALU (
    .A1(A1), .B1(B1), .B2(B2), .B3(B3), .B4(B4), .B5(B5), .B6(B6), .B7(B7), .B8(B8), .A2(A2), .A3(A3),
    .A4(A4), .A5(A5), .A6(A6), .A7(A7), .A8(A8), .SEL1(S1), .SEL2(S2), .SEL3(S3), .SEL4(S4), .Undf(ALU_undf),
    .Overf(ALU_overf), .ALU_S(ALU_alu_s));
  LED led_1 (.in(ALU_undf));
  LED led_2 (.in(ALU_overf));
  Seven_Seg_Hex seven_seg_hex_5 (.d({A4, A3, A2, A1}), .dp(1'b0));
  Register #(.Bits(8)) AC (.D(ALU_alu_s), .C(Clock), .en(en), .Q({A8, A7, A6, A5, A4, A3, A2, A1}));
  Button Enable (.out(en));
  Seven_Seg_Hex seven_seg_hex_6 (.d({A8, A7, A6, A5}), .dp(1'b0));

  // Other names for the same wires on the sheet: CLK = Clock
endmodule
