// Digital circuit incrementador-8bits.dig as structural Verilog
module incrementador_8bits (
  input  A1,
  input  A2,
  input  A3,
  input  A4,
  output S1,
  output S2,
  output S3,
  output S4
);

  wire full_adder_1bit_1_p5, full_adder_1bit_2_p5, full_adder_1bit_3_p5, full_adder_1bit_4_p5;

  // full_adder_1bit full_adder_1bit_1: pin names not known; wires that end beside it: A1, 1'b0, 1'b1, S1, full_adder_1bit_1_p5
  // full_adder_1bit full_adder_1bit_2: pin names not known; wires that end beside it: A2, 1'b0, full_adder_1bit_1_p5, S2, full_adder_1bit_2_p5
  // full_adder_1bit full_adder_1bit_3: pin names not known; wires that end beside it: A3, 1'b0, full_adder_1bit_2_p5, S3, full_adder_1bit_3_p5
  // full_adder_1bit full_adder_1bit_4: pin names not known; wires that end beside it: A4, 1'b0, full_adder_1bit_3_p5, S4, full_adder_1bit_4_p5
  LED O (.in(full_adder_1bit_4_p5));
endmodule
